# Fritzing sketch WeightScale (saved by Fritzing 0.8.5b)
breadboards: 1

parts:
  J1 = female pin header, 3 pins [form="♀ (female)"]
  J2 = female pin header, 4 pins [form="♀ (female)"]
  R1 = Resistor [tolerance=±0.1% resistance=1k package=THT]
  R2 = Resistor [tolerance=±0.1% resistance=1k package=THT]

nets:
  N1: J1.pin1, J2.pin1, R1.Pin_0
  N2: J1.pin2, J2.pin3
  N3: J1.pin3, J2.pin2, R2.Pin_1
  N4: J2.pin4, R1.Pin_1, R2.Pin_0

notes:
  Load Sensor (Black, Red, White)
  Load Cell Amplifier
  (Red, BLK, WHT, GRN)
  R1 and R2 are closely matched
